// Logisim project DEMULTIPLEXADOR.circ as structural Verilog: 1 circuit, main circuit main
module main (
  input  DADOS,
  input  S0,
  input  S1
);

  wire CLK_out, D0_out, D1_out, D2_out, D3_out;

  Button CLK (.out(CLK_out));
  and D0 (D0_out, DADOS, ~S0, ~S1);  // AND_Gate
  and D1 (D1_out, DADOS, ~S1, S0);  // AND_Gate
  and D2 (D2_out, DADOS, ~S0, S1);  // AND_Gate
  and D3 (D3_out, DADOS, S0, S1);
  // Digital_Oscilloscope digital_oscilloscope_1: pin names not known; wires that end beside it: CLK_out, DADOS, S0, S1, D0_out, D1_out, D2_out, D3_out

  // Notes on the sheet:
  //   DEMULTIPLEXADOR 1 LINHA P/ 4LINHAS
endmodule
