// Logisim project display carro.circ as structural Verilog: 5 circuits, main circuit main
module main (
  input  [3:0] Temperatura___T,
  input  [3:0] \Consumo_médio___M ,
  input  [3:0] \Consumo_Instantâneo___I ,
  input  [3:0] \Quilômetros___Q ,
  input  [1:0] in_5
);

  wire bcd_1_o0, bcd_1_o1, bcd_1_o2, bcd_1_o3, bcd_1_o4, bcd_1_o5, bcd_1_o6, bcd_1_o7, decoder_1_out0,
       decoder_1_out1, decoder_1_out2, decoder_1_out3, display7_1_o0, display7_1_o1, display7_1_o2,
       display7_1_o3, display7_1_o4, display7_1_o5, display7_1_o6, display7_2_o0, display7_2_o1,
       display7_2_o2, display7_2_o3, display7_2_o4, display7_2_o5, display7_2_o6;
  wire [3:0] multiplexer_1_out;

  Multiplexer #(.select(2), .width(4), .enable("false")) multiplexer_1 (
    .in0(Temperatura___T), .in1(\Consumo_médio___M ), .in2(\Consumo_Instantâneo___I ),
    .in3(\Quilômetros___Q ), .out(multiplexer_1_out), .sel(in_5));
  BCD bcd_1 (
    .I3(multiplexer_1_out[3]), .I2(multiplexer_1_out[2]), .I1(multiplexer_1_out[1]),
    .I0(multiplexer_1_out[0]), .O7(bcd_1_o7), .O6(bcd_1_o6), .O5(bcd_1_o5), .O4(bcd_1_o4), .O3(bcd_1_o3),
    .O2(bcd_1_o2), .O1(bcd_1_o1), .O0(bcd_1_o0));
  display7 display7_1 (
    .I3(bcd_1_o7), .I2(bcd_1_o6), .I1(bcd_1_o5), .I0(bcd_1_o4), .O6(display7_1_o6), .O5(display7_1_o5),
    .O4(display7_1_o4), .O3(display7_1_o3), .O2(display7_1_o2), .O1(display7_1_o1), .O0(display7_1_o0));
  _7_Segment_Display u_7_segment_display_1 (
    .g(display7_1_o0), .f(display7_1_o1), .a(display7_1_o6), .b(display7_1_o5), .e(display7_1_o2),
    .d(display7_1_o3), .c(display7_1_o4));  // open: dp
  LED I (.in(decoder_1_out2));
  LED M (.in(decoder_1_out1));
  LED T (.in(decoder_1_out0));
  Decoder #(.select(2), .enable("false")) decoder_1 (
    .out0(decoder_1_out0), .out1(decoder_1_out1), .out2(decoder_1_out2), .out3(decoder_1_out3), .sel(in_5));
  display7 display7_2 (
    .I3(bcd_1_o3), .I2(bcd_1_o2), .I1(bcd_1_o1), .I0(bcd_1_o0), .O6(display7_2_o6), .O5(display7_2_o5),
    .O4(display7_2_o4), .O3(display7_2_o3), .O2(display7_2_o2), .O1(display7_2_o1), .O0(display7_2_o0));
  _7_Segment_Display u_7_segment_display_2 (
    .g(display7_2_o0), .f(display7_2_o1), .a(display7_2_o6), .b(display7_2_o5), .e(display7_2_o2),
    .d(display7_2_o3), .c(display7_2_o4));  // open: dp
  LED Q (.in(decoder_1_out3));

  // Notes on the sheet:
  //   Display Multiplexado
endmodule

module display7 (
  input  I3,
  input  I2,
  input  I1,
  input  I0,
  output O6,
  output O5,
  output O4,
  output O3,
  output O2,
  output O1,
  output O0
);

  wire nand_1_out, nand_2_out, nand_3_out, nand_4_out, nand_5_out, nand_6_out, nand_7_out, nand_8_out,
       nand_9_out, nand_10_out, nand_11_out, nand_12_out, nand_13_out, nand_14_out, nand_15_out, nand_16_out,
       nand_17_out, nand_18_out, nand_19_out, nand_20_out, nand_21_out, nand_22_out, nand_23_out,
       nand_24_out, nand_25_out, nand_26_out, nand_27_out, nand_28_out, nand_29_out, nand_30_out,
       nand_31_out, nand_32_out, nand_33_out, nand_34_out, nand_35_out, nand_36_out, nand_37_out,
       nand_38_out, nand_39_out, nand_40_out, nand_41_out, nand_42_out, nand_43_out, nand_44_out,
       nand_45_out, nand_46_out, nand_47_out, nand_48_out, nand_49_out, nand_50_out, nand_51_out,
       nand_52_out, nand_53_out, nand_54_out, nand_55_out, nand_56_out, nand_57_out, nand_58_out,
       nand_59_out, nand_60_out, nand_61_out, nand_62_out, nand_63_out, nand_64_out, nand_65_out,
       nand_66_out, nand_67_out, nand_68_out, nand_69_out, nand_70_out, nand_71_out, nand_72_out,
       nand_73_out, nand_74_out, nand_75_out, nand_76_out, nand_77_out, nand_78_out;

  nand nand_1 (nand_1_out, I2, I2);
  nand nand_2 (nand_2_out, I1, I1);
  nand nand_3 (nand_3_out, I0, I0);
  nand nand_4 (nand_4_out, I3, I3);
  nand nand_5 (nand_5_out, I3, I3);
  nand nand_6 (nand_6_out, I2, I2);
  nand nand_7 (nand_7_out, I1, I1);
  nand nand_8 (nand_8_out, I3, I3);
  nand nand_9 (nand_9_out, I2, I2);
  nand nand_10 (nand_10_out, I3, I3);
  nand nand_11 (nand_11_out, I1, I1);
  nand nand_12 (nand_12_out, I0, I0);
  nand nand_13 (nand_13_out, I2, I2);
  nand nand_14 (nand_14_out, I1, I1);
  nand nand_15 (nand_15_out, I3, I3);
  nand nand_16 (nand_16_out, I2, I2);
  nand nand_17 (nand_17_out, I1, I1);
  nand nand_18 (nand_18_out, I3, I3);
  nand nand_19 (nand_19_out, I3, I3);
  nand nand_20 (nand_20_out, I3, I3);
  nand nand_21 (nand_21_out, I2, I2);
  nand nand_22 (nand_22_out, I0, I0);
  nand nand_23 (nand_23_out, I3, I3);
  nand nand_24 (nand_24_out, I2, I2);
  nand nand_25 (nand_25_out, I3, I3);
  nand nand_26 (nand_26_out, I0, I0);
  nand nand_27 (nand_27_out, I3, I3);
  nand nand_28 (nand_28_out, I1, I1);
  nand nand_29 (nand_29_out, I2, I2);
  nand nand_30 (nand_30_out, I1, I1);
  nand nand_31 (nand_31_out, I2, I2);
  nand nand_32 (nand_32_out, I1, I1);
  nand nand_33 (nand_33_out, I0, I0);
  nand nand_34 (nand_34_out, I3, I3);
  nand nand_35 (nand_35_out, I0, I0);
  nand nand_36 (nand_36_out, I3, I3);
  nand nand_37 (nand_37_out, I1, I1);
  nand nand_38 (nand_38_out, I0, I0);
  nand nand_39 (nand_39_out, I3, I3);
  nand nand_40 (nand_40_out, I1, I1);
  nand nand_41 (nand_41_out, I3, I3);
  nand nand_42 (nand_42_out, I0, I0);
  nand nand_43 (nand_43_out, I2, I2);
  nand nand_44 (nand_44_out, I1, I1);
  nand nand_45 (nand_45_out, I3, I3);
  nand nand_46 (nand_46_out, I2, I2);
  nand nand_47 (nand_47_out, I3, I3);
  nand nand_48 (nand_48_out, I1, I1);
  nand nand_49 (nand_49_out, I3, I3);
  nand nand_50 (nand_50_out, I0, I0);
  nand nand_51 (nand_51_out, I2, I2);
  nand nand_52 (nand_52_out, I1, I1);
  nand nand_53 (nand_53_out, nand_1_out, nand_2_out, nand_3_out);
  nand nand_54 (nand_54_out, nand_4_out, I1);
  nand nand_55 (nand_55_out, nand_5_out, I2, I0);
  nand nand_56 (nand_56_out, I3, nand_6_out, nand_7_out);
  nand nand_57 (nand_57_out, nand_8_out, nand_9_out);
  nand nand_58 (nand_58_out, nand_10_out, nand_11_out, nand_12_out);
  nand nand_59 (nand_59_out, nand_13_out, nand_14_out);
  nand nand_60 (nand_60_out, nand_15_out, I1, I0);
  nand nand_61 (nand_61_out, nand_16_out, nand_17_out);
  nand nand_62 (nand_62_out, nand_18_out, I0);
  nand nand_63 (nand_63_out, nand_19_out, I2);
  nand nand_64 (nand_64_out, nand_20_out, nand_21_out, nand_22_out);
  nand nand_65 (nand_65_out, nand_23_out, nand_24_out, I1);
  nand nand_66 (nand_66_out, nand_25_out, I1, nand_26_out);
  nand nand_67 (nand_67_out, nand_27_out, I2, nand_28_out, I0);
  nand nand_68 (nand_68_out, I3, nand_29_out, nand_30_out);
  nand nand_69 (nand_69_out, nand_31_out, nand_32_out, nand_33_out);
  nand nand_70 (nand_70_out, nand_34_out, I1, nand_35_out);
  nand nand_71 (nand_71_out, nand_36_out, nand_37_out, nand_38_out);
  nand nand_72 (nand_72_out, nand_39_out, I2, nand_40_out);
  nand nand_73 (nand_73_out, nand_41_out, I2, nand_42_out);
  nand nand_74 (nand_74_out, I3, nand_43_out, nand_44_out);
  nand nand_75 (nand_75_out, nand_45_out, nand_46_out, I1);
  nand nand_76 (nand_76_out, nand_47_out, I2, nand_48_out);
  nand nand_77 (nand_77_out, nand_49_out, I2, nand_50_out);
  nand nand_78 (nand_78_out, I3, nand_51_out, nand_52_out);
  nand nand_79 (O6, nand_53_out, nand_54_out, nand_55_out, nand_56_out);
  nand nand_80 (O5, nand_57_out, nand_58_out, nand_59_out, nand_60_out);
  nand nand_81 (O4, nand_61_out, nand_62_out, nand_63_out);
  nand nand_82 (O3, nand_64_out, nand_65_out, nand_66_out, nand_67_out, nand_68_out);
  nand nand_83 (O2, nand_69_out, nand_70_out);
  nand nand_84 (O1, nand_71_out, nand_72_out, nand_73_out, nand_74_out);
  nand nand_85 (O0, nand_75_out, nand_76_out, nand_77_out, nand_78_out);
endmodule

module bin_to_bcd (
  input  I3,
  input  I2,
  input  I1,
  input  I0,
  output O7,
  output O6,
  output O5,
  output O4,
  output O3,
  output O2,
  output O1,
  output O0
);

  wire and_1_out, and_2_out, and_4_out, and_5_out, and_6_out, and_7_out, not_1_out, not_2_out, not_3_out,
       not_4_out, not_5_out;

  and and_1 (and_1_out, I3, I1);
  and and_2 (and_2_out, I3, I2);
  not not_1 (not_1_out, I2);
  and and_3 (O3, I3, not_1_out, not_2_out);
  not not_2 (not_2_out, I1);
  not not_3 (not_3_out, I3);
  and and_4 (and_4_out, not_3_out, I2);
  and and_5 (and_5_out, I2, I1);
  not not_4 (not_4_out, I3);
  and and_6 (and_6_out, not_4_out, I1);
  and and_7 (and_7_out, I3, I2, not_5_out);
  not not_5 (not_5_out, I1);
  or or_1 (O4, and_1_out, and_2_out);
  or or_2 (O2, and_4_out, and_5_out);
  or or_3 (O1, and_6_out, and_7_out);

  assign O0 = I0;
  assign O5 = 1'b0;
  assign O6 = 1'b0;
  assign O7 = 1'b0;
endmodule

module BCD (
  input  I3,
  input  I2,
  input  I1,
  input  I0,
  output O7,
  output O6,
  output O5,
  output O4,
  output O3,
  output O2,
  output O1,
  output O0
);

  wire nand_1_out, nand_2_out, nand_3_out, nand_4_out, nand_5_out, nand_6_out, nand_7_out, nand_9_out,
       nand_10_out, nand_11_out, nand_12_out, nand_13_out;

  nand nand_1 (nand_1_out, I3, I1);
  nand nand_2 (nand_2_out, I3, I2);
  nand nand_3 (nand_3_out, I2, I2);
  nand nand_4 (nand_4_out, I1, I1);
  nand nand_5 (nand_5_out, I3, I3);
  nand nand_6 (nand_6_out, I3, I3);
  nand nand_7 (nand_7_out, I1, I1);
  nand nand_8 (O4, nand_1_out, nand_2_out);
  nand nand_9 (nand_9_out, I3, nand_3_out, nand_4_out);
  nand nand_10 (nand_10_out, nand_5_out, I2);
  nand nand_11 (nand_11_out, I2, I1);
  nand nand_12 (nand_12_out, nand_6_out, I1);
  nand nand_13 (nand_13_out, I3, I2, nand_7_out);
  nand nand_14 (O3, nand_9_out, nand_9_out);
  nand nand_15 (O2, nand_10_out, nand_11_out);
  nand nand_16 (O1, nand_12_out, nand_13_out);

  assign O0 = I0;
  assign O5 = 1'b0;
  assign O6 = 1'b0;
  assign O7 = 1'b0;
endmodule

module qweqw (
  input  I1,
  input  I0,
  output O3,
  output O2,
  output O1,
  output O0
);

  wire not_1_out, not_2_out, not_3_out, not_4_out;

  and and_1 (O3, I1, I0);
  not not_1 (not_1_out, I0);
  not not_2 (not_2_out, I1);
  not not_3 (not_3_out, I1);
  not not_4 (not_4_out, I0);
  and and_2 (O2, I1, not_1_out);
  and and_3 (O1, not_2_out, I0);
  and and_4 (O0, not_3_out, not_4_out);
endmodule
