// Logisim project Display_7_Segmentos.circ as structural Verilog: 2 circuits, main circuit main
module main (
  input  in_1,
  input  in_2,
  input  in_3,
  input  in_4
);

  wire display_7_1_a, display_7_1_b, display_7_1_c, display_7_1_d, display_7_1_e, display_7_1_f,
       display_7_1_g;

  Display_7 display_7_1 (
    .w(in_1), .x(in_2), .y(in_3), .z(in_4), .a(display_7_1_a), .b(display_7_1_b), .c(display_7_1_c),
    .d(display_7_1_d), .e(display_7_1_e), .f(display_7_1_f), .g(display_7_1_g));
  _7_Segment_Display u_7_segment_display_1 (
    .g(display_7_1_g), .f(display_7_1_f), .a(display_7_1_a), .b(display_7_1_b), .e(display_7_1_e),
    .d(display_7_1_d), .c(display_7_1_c));  // open: dp
endmodule

module Display_7 (
  input  w,
  input  x,
  input  y,
  input  z,
  output a,
  output b,
  output c,
  output d,
  output e,
  output f,
  output g
);

  wire nand_1_out, nand_2_out, nand_3_out, nand_4_out, nand_5_out, nand_6_out, nand_7_out, nand_8_out,
       nand_9_out, nand_10_out, nand_11_out, nand_12_out, nand_13_out, nand_14_out, nand_15_out, nand_16_out,
       nand_17_out, nand_18_out, nand_19_out, nand_20_out, nand_21_out, nand_22_out, nand_23_out,
       nand_24_out, nand_25_out, nand_26_out, nand_27_out, nand_28_out, nand_29_out, nand_30_out,
       nand_31_out, nand_32_out, nand_33_out, nand_34_out, nand_35_out, nand_36_out, nand_37_out,
       nand_38_out, nand_39_out, nand_40_out, nand_41_out, nand_42_out, nand_43_out, nand_44_out,
       nand_45_out, nand_46_out, nand_47_out, nand_48_out, nand_49_out, nand_50_out, nand_51_out,
       nand_52_out, nand_53_out, nand_54_out, nand_55_out, nand_56_out, nand_57_out, nand_58_out,
       nand_59_out, nand_60_out, nand_61_out, nand_62_out, nand_63_out, nand_64_out, nand_65_out,
       nand_66_out, nand_67_out, nand_68_out, nand_69_out, nand_70_out, nand_71_out, nand_72_out,
       nand_73_out, nand_74_out, nand_75_out, nand_76_out, nand_77_out, nand_78_out;

  nand nand_1 (nand_1_out, w, w);
  nand nand_2 (nand_2_out, x, x);
  nand nand_3 (nand_3_out, z, z);
  nand nand_4 (nand_4_out, w, w);
  nand nand_5 (nand_5_out, w, w);
  nand nand_6 (nand_6_out, x, x);
  nand nand_7 (nand_7_out, y, y);
  nand nand_8 (nand_8_out, w, w);
  nand nand_9 (nand_9_out, x, x);
  nand nand_10 (nand_10_out, w, w);
  nand nand_11 (nand_11_out, y, y);
  nand nand_12 (nand_12_out, z, z);
  nand nand_13 (nand_13_out, x, x);
  nand nand_14 (nand_14_out, y, y);
  nand nand_15 (nand_15_out, w, w);
  nand nand_16 (nand_16_out, x, x);
  nand nand_17 (nand_17_out, y, y);
  nand nand_18 (nand_18_out, w, w);
  nand nand_19 (nand_19_out, w, w);
  nand nand_20 (nand_20_out, w, w);
  nand nand_21 (nand_21_out, x, x);
  nand nand_22 (nand_22_out, z, z);
  nand nand_23 (nand_23_out, w, w);
  nand nand_24 (nand_24_out, x, x);
  nand nand_25 (nand_25_out, w, w);
  nand nand_26 (nand_26_out, z, z);
  nand nand_27 (nand_27_out, w, w);
  nand nand_28 (nand_28_out, y, y);
  nand nand_29 (nand_29_out, x, x);
  nand nand_30 (nand_30_out, y, y);
  nand nand_31 (nand_31_out, x, x);
  nand nand_32 (nand_32_out, y, y);
  nand nand_33 (nand_33_out, z, z);
  nand nand_34 (nand_34_out, w, w);
  nand nand_35 (nand_35_out, z, z);
  nand nand_36 (nand_36_out, w, w);
  nand nand_37 (nand_37_out, y, y);
  nand nand_38 (nand_38_out, z, z);
  nand nand_39 (nand_39_out, w, w);
  nand nand_40 (nand_40_out, y, y);
  nand nand_41 (nand_41_out, w, w);
  nand nand_42 (nand_42_out, z, z);
  nand nand_43 (nand_43_out, x, x);
  nand nand_44 (nand_44_out, y, y);
  nand nand_45 (nand_45_out, w, w);
  nand nand_46 (nand_46_out, x, x);
  nand nand_47 (nand_47_out, w, w);
  nand nand_48 (nand_48_out, y, y);
  nand nand_49 (nand_49_out, w, w);
  nand nand_50 (nand_50_out, z, z);
  nand nand_51 (nand_51_out, x, x);
  nand nand_52 (nand_52_out, y, y);
  nand nand_53 (nand_53_out, nand_1_out, nand_2_out, nand_3_out);
  nand nand_54 (nand_54_out, nand_4_out, y);
  nand nand_55 (nand_55_out, nand_5_out, x, z);
  nand nand_56 (nand_56_out, w, nand_6_out, nand_7_out);
  nand nand_57 (nand_57_out, nand_8_out, nand_9_out);
  nand nand_58 (nand_58_out, nand_10_out, nand_11_out, nand_12_out);
  nand nand_59 (nand_59_out, nand_13_out, nand_14_out);
  nand nand_60 (nand_60_out, nand_15_out, y, z);
  nand nand_61 (nand_61_out, nand_16_out, nand_17_out);
  nand nand_62 (nand_62_out, nand_18_out, z);
  nand nand_63 (nand_63_out, nand_19_out, x);
  nand nand_64 (nand_64_out, nand_20_out, nand_21_out, nand_22_out);
  nand nand_65 (nand_65_out, nand_23_out, nand_24_out, y);
  nand nand_66 (nand_66_out, nand_25_out, y, nand_26_out);
  nand nand_67 (nand_67_out, nand_27_out, x, nand_28_out, z);
  nand nand_68 (nand_68_out, w, nand_29_out, nand_30_out);
  nand nand_69 (nand_69_out, nand_31_out, nand_32_out, nand_33_out);
  nand nand_70 (nand_70_out, nand_34_out, y, nand_35_out);
  nand nand_71 (nand_71_out, nand_36_out, nand_37_out, nand_38_out);
  nand nand_72 (nand_72_out, nand_39_out, x, nand_40_out);
  nand nand_73 (nand_73_out, nand_41_out, x, nand_42_out);
  nand nand_74 (nand_74_out, w, nand_43_out, nand_44_out);
  nand nand_75 (nand_75_out, nand_45_out, nand_46_out, y);
  nand nand_76 (nand_76_out, nand_47_out, x, nand_48_out);
  nand nand_77 (nand_77_out, nand_49_out, x, nand_50_out);
  nand nand_78 (nand_78_out, w, nand_51_out, nand_52_out);
  nand nand_79 (a, nand_53_out, nand_54_out, nand_55_out, nand_56_out);
  nand nand_80 (b, nand_57_out, nand_58_out, nand_59_out, nand_60_out);
  nand nand_81 (c, nand_61_out, nand_62_out, nand_63_out);
  nand nand_82 (d, nand_64_out, nand_65_out, nand_66_out, nand_67_out, nand_68_out);
  nand nand_83 (e, nand_69_out, nand_70_out);
  nand nand_84 (f, nand_71_out, nand_72_out, nand_73_out, nand_74_out);
  nand nand_85 (g, nand_75_out, nand_76_out, nand_77_out, nand_78_out);
endmodule
