// Logisim project LATCH-D_CONTROLADO.circ as structural Verilog: 1 circuit, main circuit main
module main (
  input  D,
  input  EN,
  output Q,
  output out_4
);

  wire nand_1_out, nand_2_out, not_1_out;

  nand nand_1 (nand_1_out, D, EN);
  nand nand_2 (nand_2_out, EN, not_1_out);
  not not_1 (not_1_out, D);
  or or_1 (Q, ~nand_1_out, ~out_4);  // OR_Gate
  or or_2 (out_4, ~Q, ~nand_2_out);  // OR_Gate

  // Notes on the sheet:
  //    Q
endmodule
