// Logisim project LATCH-SR_CONTROLADO.circ as structural Verilog: 1 circuit, main circuit main
module main (
  input  S,
  input  EN,
  input  R,
  output Q,
  output out_5
);

  wire nand_1_out, nand_2_out;

  nand nand_1 (nand_1_out, S, EN);
  nand nand_2 (nand_2_out, EN, R);
  or or_1 (Q, ~nand_1_out, ~out_5);  // OR_Gate
  or or_2 (out_5, ~Q, ~nand_2_out);  // OR_Gate

  // Notes on the sheet:
  //   LATCH S-R CONTROLADO
  //    Q
endmodule
