// Logisim project M6 - Multiplexador para Display de 7 segmentos.circ as structural Verilog: 1 circuit, main circuit main
module main (
  input  [3:0] A,
  input  [3:0] B
);

  wire and_1_out, and_2_out, and_3_out, and_4_out, and_5_out, and_6_out, and_7_out, and_8_out, and_9_out,
       and_10_out, and_11_out, and_12_out, and_13_out, and_14_out, clock_1_out, counter_1_q, decoder_1_out0,
       decoder_1_out1, displaydecoder_1_p2, displaydecoder_1_p3, displaydecoder_1_p4, displaydecoder_1_p5,
       displaydecoder_1_p6, displaydecoder_1_p7, displaydecoder_1_p8;
  wire [3:0] multiplexer_1_out;

  Clock clock_1 (.out(clock_1_out));
  Counter #(.width(1), .max('h1)) counter_1 (
    .Q(counter_1_q), .clk(clock_1_out));  // open: load, D, count, carry, clr, preset, down
  Multiplexer #(.width(4), .enable("false")) multiplexer_1 (
    .in0(A), .in1(B), .out(multiplexer_1_out), .sel(counter_1_q));
  Decoder #(.enable("false")) decoder_1 (.out0(decoder_1_out0), .out1(decoder_1_out1), .sel(counter_1_q));
  // DisplayDecoder displaydecoder_1: pin names not known; wires that end beside it: multiplexer_1_out, displaydecoder_1_p2, displaydecoder_1_p3, displaydecoder_1_p4, displaydecoder_1_p5, displaydecoder_1_p6, displaydecoder_1_p7, displaydecoder_1_p8
  and and_1 (and_1_out, decoder_1_out1, displaydecoder_1_p8);
  _7_Segment_Display u_7_segment_display_1 (
    .g(and_1_out), .f(and_3_out), .a(and_7_out), .b(and_6_out), .e(and_2_out), .d(and_5_out), .c(and_4_out));  // open: dp
  and and_2 (and_2_out, decoder_1_out1, displaydecoder_1_p6);
  and and_3 (and_3_out, decoder_1_out1, displaydecoder_1_p7);
  and and_4 (and_4_out, decoder_1_out1, displaydecoder_1_p4);
  and and_5 (and_5_out, decoder_1_out1, displaydecoder_1_p5);
  and and_6 (and_6_out, decoder_1_out1, displaydecoder_1_p3);
  and and_7 (and_7_out, decoder_1_out1, displaydecoder_1_p2);
  and and_8 (and_8_out, displaydecoder_1_p8, decoder_1_out0);
  and and_9 (and_9_out, displaydecoder_1_p7, decoder_1_out0);
  _7_Segment_Display u_7_segment_display_2 (
    .g(and_8_out), .f(and_9_out), .a(and_14_out), .b(and_13_out), .e(and_10_out), .d(and_11_out),
    .c(and_12_out));  // open: dp
  and and_10 (and_10_out, displaydecoder_1_p6, decoder_1_out0);
  and and_11 (and_11_out, displaydecoder_1_p5, decoder_1_out0);
  and and_12 (and_12_out, displaydecoder_1_p4, decoder_1_out0);
  and and_13 (and_13_out, displaydecoder_1_p3, decoder_1_out0);
  and and_14 (and_14_out, displaydecoder_1_p2, decoder_1_out0);
endmodule
