// Logisim project M6-Demultiplexador.circ as structural Verilog: 1 circuit, main circuit main
module main (
  input  Dados,
  input  S0,
  input  S1
);

  wire button_1_out, D0_out, D1_out, D2_out, D3_out, digital_oscilloscope_1_p9, not_1_out, not_2_out;

  not not_1 (not_1_out, S0);
  not not_2 (not_2_out, S1);
  and D0 (D0_out, Dados, not_2_out, not_1_out);
  and D1 (D1_out, Dados, not_2_out, S0);
  and D2 (D2_out, Dados, S1, not_1_out);
  and D3 (D3_out, Dados, S1, S0);
  Button button_1 (.out(button_1_out));
  // Digital_Oscilloscope #(.nState(12), .frontlines("falling")) digital_oscilloscope_1: pin names not known; wires that end beside it: button_1_out, Dados, S0, S1, D0_out, D1_out, D2_out, D3_out, digital_oscilloscope_1_p9
  Button button_2 (.out(digital_oscilloscope_1_p9));

  // Notes on the sheet:
  //   Dados
  //   S0
  //   S1
  //   D0
  //   D1
  //   D2
  //   D3
endmodule
