// Logisim project M6-Multiplexadores.circ as structural Verilog
module _1_1Multiplexador4x1 (
  input  D0,
  input  D1,
  input  D2,
  input  D3,
  input  S0,
  input  S1,
  output D0_2,
  output D1_2,
  output D2_2,
  output D3_2
);

  wire clock_1_out, or_1_out;

  and and_1 (D0_2, D0, ~S0, ~S1);  // AND_Gate
  and and_2 (D1_2, D1, S0, ~S1);  // AND_Gate
  and and_3 (D2_2, D2, ~S0, S1);  // AND_Gate
  and and_4 (D3_2, D3, S0, S1);
  or or_1 (or_1_out, D0_2, D1_2, D2_2, D3_2);
  Clock clock_1 (.out(clock_1_out));
  // Digital_Oscilloscope #(.nState(9)) digital_oscilloscope_1: pin names not known; wires that end beside it: clock_1_out, D0, D1, D2, D3, S0, S1, or_1_out

  // Notes on the sheet:
  //   Entradas
  //   Seletor de Dados
  //   Saídas
  //   D0
  //   D1
  //   D2
  //   D3
  //   S0
  //   S1
  //   Saída
endmodule

module _1_2Display7SegHabilitador (
  input  [3:0] A,
  input  EN
);

  wire and_1_out, and_2_out, and_3_out, and_4_out, and_5_out, and_6_out, and_7_out, displaydecoder_1_p2,
       displaydecoder_1_p3, displaydecoder_1_p4, displaydecoder_1_p5, displaydecoder_1_p6,
       displaydecoder_1_p7, displaydecoder_1_p8;

  // DisplayDecoder displaydecoder_1: pin names not known; wires that end beside it: A, displaydecoder_1_p2, displaydecoder_1_p3, displaydecoder_1_p4, displaydecoder_1_p5, displaydecoder_1_p6, displaydecoder_1_p7, displaydecoder_1_p8
  and and_1 (and_1_out, displaydecoder_1_p8, EN);
  and and_2 (and_2_out, displaydecoder_1_p7, EN);
  _7_Segment_Display u_7_segment_display_1 (
    .g(and_1_out), .f(and_2_out), .a(and_7_out), .b(and_5_out), .e(and_4_out), .d(and_3_out), .c(and_6_out));  // open: dp
  and and_3 (and_3_out, displaydecoder_1_p5, EN);
  and and_4 (and_4_out, displaydecoder_1_p6, EN);
  and and_5 (and_5_out, displaydecoder_1_p3, EN);
  and and_6 (and_6_out, displaydecoder_1_p4, EN);
  and and_7 (and_7_out, displaydecoder_1_p2, EN);
endmodule

module Multiplexador2DisplaysDe7Segmentos (
  input  [3:0] A,
  input  [3:0] B
);

  wire and_1_out, and_2_out, and_3_out, and_4_out, and_5_out, and_6_out, and_7_out, and_8_out, and_9_out,
       and_10_out, and_11_out, and_12_out, and_13_out, and_14_out, clock_1_out, counter_1_q, decoder_1_out0,
       decoder_1_out1, displaydecoder_1_p2, displaydecoder_1_p3, displaydecoder_1_p4, displaydecoder_1_p5,
       displaydecoder_1_p6, displaydecoder_1_p7, displaydecoder_1_p8;
  wire [3:0] multiplexer_1_out;

  Multiplexer #(.width(4), .enable("false")) multiplexer_1 (
    .in0(A), .in1(B), .out(multiplexer_1_out), .sel(counter_1_q));
  Counter #(.width(1), .max('h1)) counter_1 (
    .Q(counter_1_q), .clk(clock_1_out));  // open: load, D, count, carry, clr, preset, down
  Clock clock_1 (.out(clock_1_out));
  Decoder #(.enable("false")) decoder_1 (.out0(decoder_1_out0), .out1(decoder_1_out1), .sel(counter_1_q));
  // DisplayDecoder displaydecoder_1: pin names not known; wires that end beside it: multiplexer_1_out, displaydecoder_1_p2, displaydecoder_1_p3, displaydecoder_1_p4, displaydecoder_1_p5, displaydecoder_1_p6, displaydecoder_1_p7, displaydecoder_1_p8
  and and_1 (and_1_out, displaydecoder_1_p8, decoder_1_out1);
  and and_2 (and_2_out, displaydecoder_1_p7, decoder_1_out1);
  _7_Segment_Display u_7_segment_display_1 (
    .g(and_1_out), .f(and_2_out), .a(and_8_out), .b(and_5_out), .e(and_3_out), .d(and_4_out), .c(and_6_out));  // open: dp
  and and_3 (and_3_out, displaydecoder_1_p6, decoder_1_out1);
  and and_4 (and_4_out, displaydecoder_1_p5, decoder_1_out1);
  and and_5 (and_5_out, displaydecoder_1_p3, decoder_1_out1);
  and and_6 (and_6_out, displaydecoder_1_p4, decoder_1_out1);
  and and_7 (and_7_out, displaydecoder_1_p8, decoder_1_out0);
  and and_8 (and_8_out, displaydecoder_1_p2, decoder_1_out1);
  _7_Segment_Display u_7_segment_display_2 (
    .g(and_7_out), .f(and_10_out), .a(and_13_out), .b(and_14_out), .e(and_9_out), .d(and_11_out),
    .c(and_12_out));  // open: dp
  and and_9 (and_9_out, displaydecoder_1_p6, decoder_1_out0);
  and and_10 (and_10_out, displaydecoder_1_p7, decoder_1_out0);
  and and_11 (and_11_out, displaydecoder_1_p5, decoder_1_out0);
  and and_12 (and_12_out, displaydecoder_1_p4, decoder_1_out0);
  and and_13 (and_13_out, displaydecoder_1_p2, decoder_1_out0);
  and and_14 (and_14_out, displaydecoder_1_p3, decoder_1_out0);

  // Notes on the sheet:
  //   B
  //   A
endmodule

module _4Displays7Segmentos (
  input  [3:0] A,
  input  [3:0] B,
  input  [3:0] C,
  input  [3:0] D
);

  wire and_1_out, and_2_out, and_3_out, and_4_out, and_5_out, and_6_out, and_7_out, and_8_out, and_9_out,
       and_10_out, and_11_out, and_12_out, and_13_out, and_14_out, and_15_out, and_16_out, and_17_out,
       and_18_out, and_19_out, and_20_out, and_21_out, and_22_out, and_23_out, and_24_out, and_25_out,
       and_26_out, and_27_out, and_28_out, clock_1_out, decoder_1_out0, decoder_1_out1, decoder_1_out2,
       decoder_1_out3, displaydecoder_1_p2, displaydecoder_1_p3, displaydecoder_1_p4, displaydecoder_1_p5,
       displaydecoder_1_p6, displaydecoder_1_p7, displaydecoder_1_p8;
  wire [1:0] counter_1_q;
  wire [3:0] multiplexer_1_out;

  Clock clock_1 (.out(clock_1_out));
  Multiplexer #(.select(2), .width(4), .enable("false")) multiplexer_1 (
    .in0(A), .in1(B), .in2(C), .in3(D), .out(multiplexer_1_out), .sel(counter_1_q));
  Counter #(.width(2), .max('h3)) counter_1 (
    .Q(counter_1_q), .clk(clock_1_out));  // open: load, D, count, carry, clr, preset, down
  Decoder #(.select(2), .enable("false")) decoder_1 (
    .out0(decoder_1_out0), .out1(decoder_1_out1), .out2(decoder_1_out2), .out3(decoder_1_out3),
    .sel(counter_1_q));
  // DisplayDecoder displaydecoder_1: pin names not known; wires that end beside it: multiplexer_1_out, displaydecoder_1_p2, displaydecoder_1_p3, displaydecoder_1_p4, displaydecoder_1_p5, displaydecoder_1_p6, displaydecoder_1_p7, displaydecoder_1_p8
  and and_1 (and_1_out, displaydecoder_1_p7, decoder_1_out1);
  and and_2 (and_2_out, displaydecoder_1_p8, decoder_1_out1);
  and and_3 (and_3_out, displaydecoder_1_p7, decoder_1_out3);
  and and_4 (and_4_out, displaydecoder_1_p8, decoder_1_out3);
  and and_5 (and_5_out, displaydecoder_1_p5, decoder_1_out1);
  and and_6 (and_6_out, displaydecoder_1_p6, decoder_1_out1);
  _7_Segment_Display u_7_segment_display_1 (
    .g(and_2_out), .f(and_1_out), .a(and_13_out), .b(and_10_out), .e(and_6_out), .d(and_5_out), .c(and_9_out));  // open: dp
  and and_7 (and_7_out, displaydecoder_1_p6, decoder_1_out3);
  and and_8 (and_8_out, displaydecoder_1_p5, decoder_1_out3);
  _7_Segment_Display u_7_segment_display_2 (
    .g(and_4_out), .f(and_3_out), .a(and_16_out), .b(and_11_out), .e(and_7_out), .d(and_8_out), .c(and_12_out));  // open: dp
  and and_9 (and_9_out, displaydecoder_1_p4, decoder_1_out1);
  and and_10 (and_10_out, displaydecoder_1_p3, decoder_1_out1);
  and and_11 (and_11_out, displaydecoder_1_p3, decoder_1_out3);
  and and_12 (and_12_out, displaydecoder_1_p4, decoder_1_out3);
  and and_13 (and_13_out, displaydecoder_1_p2, decoder_1_out1);
  and and_14 (and_14_out, displaydecoder_1_p8, decoder_1_out0);
  and and_15 (and_15_out, displaydecoder_1_p8, decoder_1_out2);
  and and_16 (and_16_out, displaydecoder_1_p2, decoder_1_out3);
  and and_17 (and_17_out, displaydecoder_1_p7, decoder_1_out0);
  and and_18 (and_18_out, displaydecoder_1_p6, decoder_1_out0);
  and and_19 (and_19_out, displaydecoder_1_p6, decoder_1_out2);
  and and_20 (and_20_out, displaydecoder_1_p7, decoder_1_out2);
  and and_21 (and_21_out, displaydecoder_1_p4, decoder_1_out0);
  and and_22 (and_22_out, displaydecoder_1_p5, decoder_1_out0);
  _7_Segment_Display u_7_segment_display_3 (
    .g(and_14_out), .f(and_17_out), .a(and_26_out), .b(and_25_out), .e(and_18_out), .d(and_22_out),
    .c(and_21_out));  // open: dp
  and and_23 (and_23_out, displaydecoder_1_p4, decoder_1_out2);
  and and_24 (and_24_out, displaydecoder_1_p5, decoder_1_out2);
  _7_Segment_Display u_7_segment_display_4 (
    .g(and_15_out), .f(and_20_out), .a(and_27_out), .b(and_28_out), .e(and_19_out), .d(and_24_out),
    .c(and_23_out));  // open: dp
  and and_25 (and_25_out, displaydecoder_1_p3, decoder_1_out0);
  and and_26 (and_26_out, displaydecoder_1_p2, decoder_1_out0);
  and and_27 (and_27_out, displaydecoder_1_p2, decoder_1_out2);
  and and_28 (and_28_out, displaydecoder_1_p3, decoder_1_out2);

  // Notes on the sheet:
  //   B
  //   D
  //   A
  //   C
endmodule
