// Logisim project MULTIPLEXADORES.circ as structural Verilog: 1 circuit, main circuit main
module main (
  input  S1,
  input  S0,
  input  D0,
  input  D1,
  input  D2,
  input  D3,
  input  E,
  input  [3:0] A,
  input  [3:0] A_2,
  input  [3:0] B,
  input  [3:0] C,
  input  [3:0] B_2,
  input  [3:0] D,
  output out_14,
  output [3:0] A_3
);

  wire and_1_out, and_2_out, and_3_out, and_4_out, and_5_out, and_6_out, and_7_out, and_8_out, and_9_out,
       and_10_out, and_11_out, and_12_out, and_13_out, and_14_out, and_15_out, and_16_out, and_17_out,
       and_18_out, and_19_out, and_20_out, and_21_out, and_22_out, and_23_out, and_24_out, and_25_out,
       and_26_out, and_27_out, and_28_out, and_29_out, and_30_out, and_31_out, and_32_out, and_33_out,
       and_34_out, and_35_out, and_36_out, and_37_out, and_38_out, and_39_out, and_40_out, and_41_out,
       and_42_out, and_43_out, and_44_out, and_45_out, and_46_out, and_47_out, and_48_out, and_49_out,
       and_50_out, and_51_out, and_52_out, and_53_out, button_1_out, CLK_out, clock_1_out, clock_2_out,
       clock_3_out, counter_2_q, decoder_1_out0, decoder_1_out1, decoder_2_out0, decoder_2_out1,
       decoder_2_out2, decoder_2_out3, displaydecoder_1_p2, displaydecoder_1_p3, displaydecoder_1_p4,
       displaydecoder_1_p5, displaydecoder_1_p6, displaydecoder_1_p7, displaydecoder_1_p8,
       displaydecoder_2_p2, displaydecoder_2_p3, displaydecoder_2_p4, displaydecoder_2_p5,
       displaydecoder_2_p6, displaydecoder_2_p7, displaydecoder_2_p8, displaydecoder_3_p2,
       displaydecoder_3_p3, displaydecoder_3_p4, displaydecoder_3_p5, displaydecoder_3_p6,
       displaydecoder_3_p7, displaydecoder_3_p8;
  wire [1:0] counter_3_q;
  wire [3:0] multiplexer_1_out, multiplexer_2_out;

  Button CLK (.out(CLK_out));
  Clock clock_1 (.out(clock_1_out));
  Button button_1 (.out(button_1_out));
  Clock clock_2 (.out(clock_2_out));
  Counter #(.width(4), .max('hf)) counter_1 (
    .Q(A_3), .clk(clock_1_out), .clr(button_1_out));  // open: load, D, count, carry, preset, down
  Multiplexer #(.width(4), .enable("false")) multiplexer_1 (
    .in0(A_2), .in1(B_2), .out(multiplexer_1_out), .sel(counter_2_q));
  Counter #(.width(1), .max('h1)) counter_2 (
    .Q(counter_2_q), .clk(clock_2_out));  // open: load, D, count, carry, clr, preset, down
  and and_1 (and_1_out, D0, ~S1, ~S0);  // AND_Gate
  and and_2 (and_2_out, D1, S0, ~S1);  // AND_Gate
  and and_3 (and_3_out, D2, S1, ~S0);  // AND_Gate
  and and_4 (and_4_out, D3, S0, S1);
  // DisplayDecoder displaydecoder_1: pin names not known; wires that end beside it: A_3, displaydecoder_1_p2, displaydecoder_1_p3, displaydecoder_1_p4, displaydecoder_1_p5, displaydecoder_1_p6, displaydecoder_1_p7, displaydecoder_1_p8
  // DisplayDecoder displaydecoder_2: pin names not known; wires that end beside it: multiplexer_1_out, displaydecoder_2_p2, displaydecoder_2_p3, displaydecoder_2_p4, displaydecoder_2_p5, displaydecoder_2_p6, displaydecoder_2_p7, displaydecoder_2_p8
  Decoder #(.enable("false")) decoder_1 (.out0(decoder_1_out0), .out1(decoder_1_out1), .sel(counter_2_q));
  or or_1 (out_14, and_1_out, and_2_out, and_3_out, and_4_out);
  and and_5 (and_5_out, displaydecoder_1_p8, E);
  and and_6 (and_6_out, displaydecoder_1_p7, E);
  _7_Segment_Display u_7_segment_display_1 (
    .g(and_5_out), .f(and_6_out), .a(and_17_out), .b(and_13_out), .e(and_10_out), .d(and_9_out),
    .c(and_14_out));  // open: dp
  and and_7 (and_7_out, decoder_1_out1, displaydecoder_2_p7);
  and and_8 (and_8_out, decoder_1_out1, displaydecoder_2_p8);
  _7_Segment_Display u_7_segment_display_2 (
    .g(and_8_out), .f(and_7_out), .a(and_18_out), .b(and_16_out), .e(and_12_out), .d(and_11_out),
    .c(and_15_out));  // open: dp
  and and_9 (and_9_out, displaydecoder_1_p5, E);
  and and_10 (and_10_out, displaydecoder_1_p6, E);
  and and_11 (and_11_out, decoder_1_out1, displaydecoder_2_p5);
  and and_12 (and_12_out, decoder_1_out1, displaydecoder_2_p6);
  // Digital_Oscilloscope digital_oscilloscope_1: pin names not known; wires that end beside it: CLK_out, D0, D1, D2, D3, S0, S1, out_14
  and and_13 (and_13_out, displaydecoder_1_p3, E);
  and and_14 (and_14_out, displaydecoder_1_p4, E);
  and and_15 (and_15_out, decoder_1_out1, displaydecoder_2_p4);
  and and_16 (and_16_out, decoder_1_out1, displaydecoder_2_p3);
  and and_17 (and_17_out, displaydecoder_1_p2, E);
  and and_18 (and_18_out, decoder_1_out1, displaydecoder_2_p2);
  and and_19 (and_19_out, displaydecoder_2_p8, decoder_1_out0);
  _7_Segment_Display u_7_segment_display_3 (
    .g(and_19_out), .f(and_20_out), .a(and_25_out), .b(and_24_out), .e(and_21_out), .d(and_22_out),
    .c(and_23_out));  // open: dp
  and and_20 (and_20_out, displaydecoder_2_p7, decoder_1_out0);
  and and_21 (and_21_out, displaydecoder_2_p6, decoder_1_out0);
  and and_22 (and_22_out, displaydecoder_2_p5, decoder_1_out0);
  and and_23 (and_23_out, displaydecoder_2_p4, decoder_1_out0);
  and and_24 (and_24_out, displaydecoder_2_p3, decoder_1_out0);
  and and_25 (and_25_out, displaydecoder_2_p2, decoder_1_out0);
  Clock clock_3 (.out(clock_3_out));
  Multiplexer #(.select(2), .width(4), .enable("false")) multiplexer_2 (
    .in0(A), .in1(B), .in2(C), .in3(D), .out(multiplexer_2_out), .sel(counter_3_q));
  Counter #(.width(2), .max('h4)) counter_3 (
    .Q(counter_3_q), .clk(clock_3_out));  // open: load, D, count, carry, clr, preset, down
  // DisplayDecoder displaydecoder_3: pin names not known; wires that end beside it: multiplexer_2_out, displaydecoder_3_p2, displaydecoder_3_p3, displaydecoder_3_p4, displaydecoder_3_p5, displaydecoder_3_p6, displaydecoder_3_p7, displaydecoder_3_p8
  Decoder #(.select(2), .enable("false")) decoder_2 (
    .out0(decoder_2_out0), .out1(decoder_2_out1), .out2(decoder_2_out2), .out3(decoder_2_out3),
    .sel(counter_3_q));
  and and_26 (and_26_out, decoder_2_out3, displaydecoder_3_p8);
  _7_Segment_Display u_7_segment_display_4 (
    .g(and_26_out), .f(and_27_out), .a(and_32_out), .b(and_31_out), .e(and_28_out), .d(and_29_out),
    .c(and_30_out));  // open: dp
  and and_27 (and_27_out, decoder_2_out3, displaydecoder_3_p7);
  and and_28 (and_28_out, decoder_2_out3, displaydecoder_3_p6);
  and and_29 (and_29_out, decoder_2_out3, displaydecoder_3_p5);
  and and_30 (and_30_out, decoder_2_out3, displaydecoder_3_p4);
  and and_31 (and_31_out, decoder_2_out3, displaydecoder_3_p3);
  and and_32 (and_32_out, decoder_2_out3, displaydecoder_3_p2);
  and and_33 (and_33_out, decoder_2_out2, displaydecoder_3_p7);
  and and_34 (and_34_out, decoder_2_out2, displaydecoder_3_p8);
  _7_Segment_Display u_7_segment_display_5 (
    .g(and_34_out), .f(and_33_out), .a(and_39_out), .b(and_37_out), .e(and_35_out), .d(and_36_out),
    .c(and_38_out));  // open: dp
  and and_35 (and_35_out, decoder_2_out2, displaydecoder_3_p6);
  and and_36 (and_36_out, decoder_2_out2, displaydecoder_3_p5);
  and and_37 (and_37_out, decoder_2_out2, displaydecoder_3_p3);
  and and_38 (and_38_out, decoder_2_out2, displaydecoder_3_p4);
  and and_39 (and_39_out, decoder_2_out2, displaydecoder_3_p2);
  and and_40 (and_40_out, decoder_2_out1, displaydecoder_3_p7);
  and and_41 (and_41_out, decoder_2_out1, displaydecoder_3_p8);
  _7_Segment_Display u_7_segment_display_6 (
    .g(and_41_out), .f(and_40_out), .a(and_47_out), .b(and_44_out), .e(and_42_out), .d(and_43_out),
    .c(and_45_out));  // open: dp
  and and_42 (and_42_out, decoder_2_out1, displaydecoder_3_p6);
  and and_43 (and_43_out, decoder_2_out1, displaydecoder_3_p5);
  and and_44 (and_44_out, decoder_2_out1, displaydecoder_3_p3);
  and and_45 (and_45_out, decoder_2_out1, displaydecoder_3_p4);
  and and_46 (and_46_out, displaydecoder_3_p8, decoder_2_out0);
  and and_47 (and_47_out, decoder_2_out1, displaydecoder_3_p2);
  _7_Segment_Display u_7_segment_display_7 (
    .g(and_46_out), .f(and_49_out), .a(and_52_out), .b(and_53_out), .e(and_48_out), .d(and_50_out),
    .c(and_51_out));  // open: dp
  and and_48 (and_48_out, displaydecoder_3_p6, decoder_2_out0);
  and and_49 (and_49_out, displaydecoder_3_p7, decoder_2_out0);
  and and_50 (and_50_out, displaydecoder_3_p5, decoder_2_out0);
  and and_51 (and_51_out, displaydecoder_3_p4, decoder_2_out0);
  and and_52 (and_52_out, displaydecoder_3_p2, decoder_2_out0);
  and and_53 (and_53_out, displaydecoder_3_p3, decoder_2_out0);

  // Notes on the sheet:
  //   MULTPLEXADOR 1 BIT
  //   DISPLAY DE 7 SEGMENTOS COM HABILITADOR
  //   MULTIPLEXADOR PARA 2 DISPLAY DE 7 SEGMENTOS
  //   MULTIPLEXADOR PARA 4 DISPLAY DE 7 SEGMENTOS
endmodule
