// Logisim project Processador_3_instrucoes.circ as structural Verilog: 7 circuits, main circuit main
module main (
  output [15:0] out_1,
  output [15:0] out_2,
  output [3:0] out_3
);

  wire and_1_out, clk, clr, or_1_out, or_2_out, unidadecontrole_1_alu_s0, unidadecontrole_1_d_rd,
       unidadecontrole_1_d_wr, unidadecontrole_1_i_rd, unidadecontrole_1_ir_ld, unidadecontrole_1_pc_clr,
       unidadecontrole_1_pc_inc, unidadecontrole_1_rf_rp_rd, unidadecontrole_1_rf_rq_rd,
       unidadecontrole_1_rf_s, unidadecontrole_1_rf_w_wr;
  wire [3:0] IR_q, IR_q_2, IR_q_3, IR_q_4, PC_q, unidadecontrole_1_rf_rp_addr, unidadecontrole_1_rf_rq_addr;
  wire [7:0] unidadecontrole_1_d_addr;
  wire [15:0] adder_1_out, multiplexer_1_out, ram_2_dout, rf_1_rp_data, rf_1_rq_data;

  or or_1 (or_1_out, clr, clk);
  RAM #(.addrWidth(4), .dataWidth(16)) ram_1 (
    .addr(PC_q), .oe(or_2_out), .clk(or_1_out), .dout(out_1));  // open: we, din
  or or_2 (or_2_out, clr, unidadecontrole_1_i_rd);
  Button button_1 (.out(clr));
  Clock clock_1 (.out(clk));
  Counter #(.max('hf), .width(4)) PC (
    .Q(PC_q), .clk(and_1_out), .clr(unidadecontrole_1_pc_clr));  // open: load, D, count, carry, up
  and and_1 (and_1_out, 1'b1, unidadecontrole_1_pc_inc);
  UnidadeControle unidadecontrole_1 (
    .d({IR_q_2, IR_q}), .op(IR_q_4), .ra(IR_q_3), .rb(IR_q_2), .rc(IR_q), .clk(clk), .clr(clr),
    .D_addr(unidadecontrole_1_d_addr), .RF_W_addr(out_3), .RF_Rp_addr(unidadecontrole_1_rf_rp_addr),
    .RF_Rq_addr(unidadecontrole_1_rf_rq_addr), .PC_clr(unidadecontrole_1_pc_clr),
    .I_rd(unidadecontrole_1_i_rd), .PC_inc(unidadecontrole_1_pc_inc), .IR_ld(unidadecontrole_1_ir_ld),
    .D_rd(unidadecontrole_1_d_rd), .RF_s(unidadecontrole_1_rf_s), .RF_W_wr(unidadecontrole_1_rf_w_wr),
    .D_wr(unidadecontrole_1_d_wr), .RF_Rp_rd(unidadecontrole_1_rf_rp_rd),
    .RF_Rq_rd(unidadecontrole_1_rf_rq_rd), .alu_s0(unidadecontrole_1_alu_s0));
  Multiplexer #(.width(16)) multiplexer_1 (
    .in0({16{1'b0}}), .in1(adder_1_out), .out(multiplexer_1_out), .sel(unidadecontrole_1_alu_s0));
  Register #(.width(16)) IR (
    .D(out_1), .en(unidadecontrole_1_ir_ld), .clk(clk), .Q({IR_q_4, IR_q_3, IR_q_2, IR_q}), .clr(clr));
  Multiplexer #(.width(16)) multiplexer_2 (
    .in0(multiplexer_1_out), .in1(ram_2_dout), .out(out_2), .sel(unidadecontrole_1_rf_s));
  Adder #(.width(16)) adder_1 (.a(rf_1_rq_data), .b(rf_1_rp_data), .out(adder_1_out));  // open: cin, cout
  RF rf_1 (
    .Rp_rd(unidadecontrole_1_rf_rp_rd), .Rp_addr(unidadecontrole_1_rf_rp_addr), .W_data(out_2), .clr(clr),
    .Rq_rd(unidadecontrole_1_rf_rq_rd), .Rq_addr(unidadecontrole_1_rf_rq_addr), .clk(clk),
    .W_wr(unidadecontrole_1_rf_w_wr), .W_addr(out_3), .Rp_data(rf_1_rp_data), .Rq_data(rf_1_rq_data));
  RAM #(.dataWidth(16), .trigger("falling")) ram_2 (
    .addr(unidadecontrole_1_d_addr), .we(unidadecontrole_1_d_wr), .oe(unidadecontrole_1_d_rd), .clk(clk),
    .din(rf_1_rp_data), .dout(ram_2_dout));
endmodule

module Operacional (
  input  [7:0] S1,
  input  [7:0] S2,
  output [7:0] Sout
);

  Adder adder_1 (.a(S1), .b(S2), .out(Sout));  // open: cin, cout
endmodule

module RegisterBank (
  input  [2:0] Rd_addr,
  input  [15:0] W_data,
  input  Rd_en,
  input  clr,
  input  clk,
  input  [2:0] W_addr,
  input  W_en,
  output [15:0] R_data
);

  wire decoder_1_out0, decoder_1_out1, decoder_1_out2, decoder_1_out3, decoder_1_out4, decoder_1_out5,
       decoder_1_out6, decoder_1_out7, decoder_2_out0, decoder_2_out1, decoder_2_out2, decoder_2_out3,
       decoder_2_out4, decoder_2_out5, decoder_2_out6, decoder_2_out7;
  wire [15:0] register_1_q, register_2_q, register_3_q, register_4_q, register_5_q, register_6_q,
       register_7_q, register_8_q;

  Decoder #(.select(3)) decoder_1 (
    .out0(decoder_1_out0), .out1(decoder_1_out1), .out2(decoder_1_out2), .out3(decoder_1_out3),
    .out4(decoder_1_out4), .out5(decoder_1_out5), .out6(decoder_1_out6), .out7(decoder_1_out7), .sel(W_addr),
    .en(W_en));
  Register #(.width(16)) register_1 (.D(W_data), .en(decoder_1_out0), .clk(clk), .Q(register_1_q), .clr(clr));
  Register #(.width(16)) register_2 (.D(W_data), .en(decoder_1_out1), .clk(clk), .Q(register_2_q), .clr(clr));
  Register #(.width(16)) register_3 (.en(decoder_1_out2), .clk(clk), .Q(register_3_q), .clr(clr));  // open: D
  Register #(.width(16)) register_4 (.D(W_data), .en(decoder_1_out3), .clk(clk), .Q(register_4_q), .clr(clr));
  Register #(.width(16)) register_5 (.D(W_data), .en(decoder_1_out4), .clk(clk), .Q(register_5_q), .clr(clr));
  Register #(.width(16)) register_6 (.D(W_data), .en(decoder_1_out5), .clk(clk), .Q(register_6_q), .clr(clr));
  Register #(.width(16)) register_7 (.D(W_data), .en(decoder_1_out6), .clk(clk), .Q(register_7_q), .clr(clr));
  Register #(.width(16)) register_8 (.D(W_data), .en(decoder_1_out7), .clk(clk), .Q(register_8_q), .clr(clr));
  assign R_data = decoder_2_out0 ? register_1_q : 16'bz;  // Controlled_Buffer controlled_buffer_1
  assign R_data = decoder_2_out1 ? register_2_q : 16'bz;  // Controlled_Buffer controlled_buffer_2
  assign R_data = decoder_2_out2 ? register_3_q : 16'bz;  // Controlled_Buffer controlled_buffer_3
  assign R_data = decoder_2_out3 ? register_4_q : 16'bz;  // Controlled_Buffer controlled_buffer_4
  assign R_data = decoder_2_out4 ? register_5_q : 16'bz;  // Controlled_Buffer controlled_buffer_5
  assign R_data = decoder_2_out5 ? register_6_q : 16'bz;  // Controlled_Buffer controlled_buffer_6
  assign R_data = decoder_2_out6 ? register_7_q : 16'bz;  // Controlled_Buffer controlled_buffer_7
  assign R_data = decoder_2_out7 ? register_8_q : 16'bz;  // Controlled_Buffer controlled_buffer_8
  Decoder #(.select(3)) decoder_2 (
    .out0(decoder_2_out0), .out1(decoder_2_out1), .out2(decoder_2_out2), .out3(decoder_2_out3),
    .out4(decoder_2_out4), .out5(decoder_2_out5), .out6(decoder_2_out6), .out7(decoder_2_out7),
    .sel(Rd_addr), .en(Rd_en));
endmodule

module UnidadeDeControle (
  input  [7:0] d,
  input  [3:0] ra,
  input  [3:0] rc,
  input  [1:0] op,
  input  clr,
  input  [3:0] rb,
  input  clk,
  output [7:0] D_addr,
  output [3:0] RF_W_addr,
  output PC_clr,
  output I_rd,
  output D_wr,
  output PC_inc,
  output RF_Rp_rd,
  output IR_ld,
  output D_rd,
  output [3:0] RF_Rp_addr,
  output RF_W_wr,
  output RF_s,
  output [3:0] RF_Rq_addr,
  output RF_Rq_rd,
  output alu_s0
);

  wire dc, dc1, dc2, dc3, multiplexer_4_out, or_1_out, or_2_out, or_3_out, or_6_out, or_7_out, or_8_out;
  wire [2:0] multiplexer_1_out, multiplexer_2_out, register_1_q;
  wire [3:0] demultiplexer_1_out1, register_3_q, register_4_q;

  Register #(.width(3)) register_1 (.D(multiplexer_2_out), .clk(clk), .Q(register_1_q), .clr(clr));  // open: en
  Decoder #(.select(3)) decoder_1 (
    .out0(PC_clr), .out1(I_rd), .out2(dc), .out3(D_rd), .out4(D_wr), .out5(alu_s0), .sel(register_1_q));  // open: out6, out7, en
  Multiplexer #(.select(2), .width(3)) multiplexer_1 (
    .in0(3'b011), .in1(3'b100), .in2(3'b101), .out(multiplexer_1_out), .sel(op));  // open: in3
  or or_1 (or_1_out, alu_s0, dc3);
  Register register_2 (.D(d), .en(or_2_out), .clk(clk), .Q(D_addr), .clr(clr));
  or or_2 (or_2_out, D_wr, D_rd, dc1, dc2);
  Register #(.width(4)) register_3 (.D(ra), .en(or_3_out), .clk(clk), .Q(register_3_q), .clr(clr));
  or or_3 (or_3_out, or_2_out, dc);
  and and_1 (dc1, ~op[1], ~op[0], dc);  // AND_Gate
  and and_2 (dc2, ~op[1], op[0], dc);  // AND_Gate
  and and_3 (dc3, op[1], ~op[0], dc);  // AND_Gate
  or or_4 (RF_W_wr, D_rd, alu_s0);
  Multiplexer #(.select(3), .width(3)) multiplexer_2 (
    .in0(3'b001), .in1(3'b010), .in2(multiplexer_1_out), .in3(3'b001), .in4(3'b001), .in5(3'b001),
    .out(multiplexer_2_out), .sel(register_1_q));  // open: in6, in7
  Register #(.width(4)) register_4 (.D(rb), .en(or_1_out), .clk(clk), .Q(register_4_q), .clr(clr));
  Demultiplexer #(.width(4)) demultiplexer_1 (
    .out0(RF_W_addr), .out1(demultiplexer_1_out1), .in(register_3_q), .sel(D_wr));
  Multiplexer #(.width(4)) multiplexer_3 (
    .in0(demultiplexer_1_out1), .in1(register_4_q), .out(RF_Rp_addr), .sel(alu_s0));
  or or_5 (RF_Rp_rd, D_wr, alu_s0);
  or or_6 (or_6_out, D_rd, alu_s0, dc3);
  or or_7 (or_7_out, dc3, alu_s0);
  Register #(.width(4)) register_5 (.D(rc), .en(or_8_out), .clk(clk), .Q(RF_Rq_addr), .clr(clr));
  or or_8 (or_8_out, alu_s0, dc3);
  Multiplexer multiplexer_4 (.in0(1'b1), .in1(1'b0), .out(multiplexer_4_out), .sel(or_7_out));
  Register #(.width(1)) register_6 (.D(multiplexer_4_out), .en(or_6_out), .clk(clk), .Q(RF_s), .clr(clr));

  assign IR_ld = I_rd;
  assign PC_inc = I_rd;
  assign RF_Rq_rd = alu_s0;
endmodule

module RF (
  input  Rp_rd,
  input  [3:0] Rp_addr,
  input  [15:0] W_data,
  input  clr,
  input  Rq_rd,
  input  [3:0] Rq_addr,
  input  clk,
  input  W_wr,
  input  [3:0] W_addr,
  output [15:0] Rp_data,
  output [15:0] Rq_data
);

  wire decoder_1_out0, decoder_1_out1, decoder_1_out2, decoder_1_out3, decoder_1_out4, decoder_1_out5,
       decoder_1_out6, decoder_1_out7, decoder_1_out8, decoder_1_out9, decoder_1_out10, decoder_1_out11,
       decoder_1_out12, decoder_1_out13, decoder_1_out14, decoder_1_out15, decoder_2_out0, decoder_2_out1,
       decoder_2_out2, decoder_2_out3, decoder_2_out4, decoder_2_out5, decoder_2_out6, decoder_2_out7,
       decoder_2_out8, decoder_2_out9, decoder_2_out10, decoder_2_out11, decoder_2_out12, decoder_2_out13,
       decoder_2_out14, decoder_2_out15, decoder_3_out0, decoder_3_out1, decoder_3_out2, decoder_3_out3,
       decoder_3_out4, decoder_3_out5, decoder_3_out6, decoder_3_out7, decoder_3_out8, decoder_3_out9,
       decoder_3_out10, decoder_3_out11, decoder_3_out12, decoder_3_out13, decoder_3_out14, decoder_3_out15;
  wire [15:0] register_1_q, register_2_q, register_3_q, register_4_q, register_5_q, register_6_q,
       register_7_q, register_8_q, register_9_q, register_10_q, register_11_q, register_12_q, register_13_q,
       register_14_q, register_15_q, register_16_q;

  Decoder #(.select(4)) decoder_1 (
    .out0(decoder_1_out0), .out1(decoder_1_out1), .out2(decoder_1_out2), .out3(decoder_1_out3),
    .out4(decoder_1_out4), .out5(decoder_1_out5), .out6(decoder_1_out6), .out7(decoder_1_out7),
    .out8(decoder_1_out8), .out9(decoder_1_out9), .out10(decoder_1_out10), .out11(decoder_1_out11),
    .out12(decoder_1_out12), .out13(decoder_1_out13), .out14(decoder_1_out14), .out15(decoder_1_out15),
    .sel(W_addr), .en(W_wr));
  Register #(.width(16)) register_1 (.D(W_data), .en(decoder_1_out0), .clk(clk), .Q(register_1_q), .clr(clr));
  Register #(.width(16)) register_2 (.D(W_data), .en(decoder_1_out1), .clk(clk), .Q(register_2_q), .clr(clr));
  Register #(.width(16)) register_3 (.D(W_data), .en(decoder_1_out2), .clk(clk), .Q(register_3_q), .clr(clr));
  Register #(.width(16)) register_4 (.D(W_data), .en(decoder_1_out3), .clk(clk), .Q(register_4_q), .clr(clr));
  Register #(.width(16)) register_5 (.D(W_data), .en(decoder_1_out4), .clk(clk), .Q(register_5_q), .clr(clr));
  Register #(.width(16)) register_6 (.D(W_data), .en(decoder_1_out5), .clk(clk), .Q(register_6_q), .clr(clr));
  Register #(.width(16)) register_7 (.D(W_data), .en(decoder_1_out6), .clk(clk), .Q(register_7_q), .clr(clr));
  Register #(.width(16)) register_8 (.D(W_data), .en(decoder_1_out7), .clk(clk), .Q(register_8_q), .clr(clr));
  Register #(.width(16)) register_9 (.D(W_data), .en(decoder_1_out8), .clk(clk), .Q(register_9_q), .clr(clr));
  Register #(.width(16)) register_10 (.D(W_data), .en(decoder_1_out9), .clk(clk), .Q(register_10_q), .clr(clr));
  Register #(.width(16)) register_11 (.D(W_data), .en(decoder_1_out10), .clk(clk), .Q(register_11_q), .clr(clr));
  Register #(.width(16)) register_12 (.D(W_data), .en(decoder_1_out11), .clk(clk), .Q(register_12_q), .clr(clr));
  Register #(.width(16)) register_13 (.D(W_data), .en(decoder_1_out12), .clk(clk), .Q(register_13_q), .clr(clr));
  Register #(.width(16)) register_14 (.D(W_data), .en(decoder_1_out13), .clk(clk), .Q(register_14_q), .clr(clr));
  Register #(.width(16)) register_15 (.D(W_data), .en(decoder_1_out14), .clk(clk), .Q(register_15_q), .clr(clr));
  Register #(.width(16)) register_16 (.D(W_data), .en(decoder_1_out15), .clk(clk), .Q(register_16_q), .clr(clr));
  assign Rq_data = decoder_2_out0 ? register_1_q : 16'bz;  // Controlled_Buffer controlled_buffer_1
  assign Rq_data = decoder_2_out1 ? register_2_q : 16'bz;  // Controlled_Buffer controlled_buffer_2
  assign Rq_data = decoder_2_out2 ? register_3_q : 16'bz;  // Controlled_Buffer controlled_buffer_3
  assign Rq_data = decoder_2_out3 ? register_4_q : 16'bz;  // Controlled_Buffer controlled_buffer_4
  assign Rq_data = decoder_2_out4 ? register_5_q : 16'bz;  // Controlled_Buffer controlled_buffer_5
  assign Rq_data = decoder_2_out5 ? register_6_q : 16'bz;  // Controlled_Buffer controlled_buffer_6
  assign Rq_data = decoder_2_out6 ? register_7_q : 16'bz;  // Controlled_Buffer controlled_buffer_7
  assign Rq_data = decoder_2_out7 ? register_8_q : 16'bz;  // Controlled_Buffer controlled_buffer_8
  assign Rq_data = decoder_2_out8 ? register_9_q : 16'bz;  // Controlled_Buffer controlled_buffer_9
  assign Rq_data = decoder_2_out9 ? register_10_q : 16'bz;  // Controlled_Buffer controlled_buffer_10
  assign Rq_data = decoder_2_out10 ? register_11_q : 16'bz;  // Controlled_Buffer controlled_buffer_11
  assign Rq_data = decoder_2_out11 ? register_12_q : 16'bz;  // Controlled_Buffer controlled_buffer_12
  assign Rq_data = decoder_2_out12 ? register_13_q : 16'bz;  // Controlled_Buffer controlled_buffer_13
  assign Rq_data = decoder_2_out13 ? register_14_q : 16'bz;  // Controlled_Buffer controlled_buffer_14
  assign Rq_data = decoder_2_out14 ? register_15_q : 16'bz;  // Controlled_Buffer controlled_buffer_15
  assign Rq_data = decoder_2_out15 ? register_16_q : 16'bz;  // Controlled_Buffer controlled_buffer_16
  assign Rp_data = decoder_3_out0 ? register_1_q : 16'bz;  // Controlled_Buffer controlled_buffer_17
  assign Rp_data = decoder_3_out1 ? register_2_q : 16'bz;  // Controlled_Buffer controlled_buffer_18
  assign Rp_data = decoder_3_out2 ? register_3_q : 16'bz;  // Controlled_Buffer controlled_buffer_19
  assign Rp_data = decoder_3_out3 ? register_4_q : 16'bz;  // Controlled_Buffer controlled_buffer_20
  assign Rp_data = decoder_3_out4 ? register_5_q : 16'bz;  // Controlled_Buffer controlled_buffer_21
  assign Rp_data = decoder_3_out5 ? register_6_q : 16'bz;  // Controlled_Buffer controlled_buffer_22
  assign Rp_data = decoder_3_out6 ? register_7_q : 16'bz;  // Controlled_Buffer controlled_buffer_23
  assign Rp_data = decoder_3_out7 ? register_8_q : 16'bz;  // Controlled_Buffer controlled_buffer_24
  assign Rp_data = decoder_3_out8 ? register_9_q : 16'bz;  // Controlled_Buffer controlled_buffer_25
  assign Rp_data = decoder_3_out9 ? register_10_q : 16'bz;  // Controlled_Buffer controlled_buffer_26
  assign Rp_data = decoder_3_out10 ? register_11_q : 16'bz;  // Controlled_Buffer controlled_buffer_27
  assign Rp_data = decoder_3_out11 ? register_12_q : 16'bz;  // Controlled_Buffer controlled_buffer_28
  assign Rp_data = decoder_3_out12 ? register_13_q : 16'bz;  // Controlled_Buffer controlled_buffer_29
  assign Rp_data = decoder_3_out13 ? register_14_q : 16'bz;  // Controlled_Buffer controlled_buffer_30
  assign Rp_data = decoder_3_out14 ? register_15_q : 16'bz;  // Controlled_Buffer controlled_buffer_31
  assign Rp_data = decoder_3_out15 ? register_16_q : 16'bz;  // Controlled_Buffer controlled_buffer_32
  Decoder #(.select(4)) decoder_2 (
    .out0(decoder_2_out0), .out1(decoder_2_out1), .out2(decoder_2_out2), .out3(decoder_2_out3),
    .out4(decoder_2_out4), .out5(decoder_2_out5), .out6(decoder_2_out6), .out7(decoder_2_out7),
    .out8(decoder_2_out8), .out9(decoder_2_out9), .out10(decoder_2_out10), .out11(decoder_2_out11),
    .out12(decoder_2_out12), .out13(decoder_2_out13), .out14(decoder_2_out14), .out15(decoder_2_out15),
    .sel(Rq_addr), .en(Rq_rd));
  Decoder #(.select(4)) decoder_3 (
    .out0(decoder_3_out0), .out1(decoder_3_out1), .out2(decoder_3_out2), .out3(decoder_3_out3),
    .out4(decoder_3_out4), .out5(decoder_3_out5), .out6(decoder_3_out6), .out7(decoder_3_out7),
    .out8(decoder_3_out8), .out9(decoder_3_out9), .out10(decoder_3_out10), .out11(decoder_3_out11),
    .out12(decoder_3_out12), .out13(decoder_3_out13), .out14(decoder_3_out14), .out15(decoder_3_out15),
    .sel(Rp_addr), .en(Rp_rd));
endmodule

module FSMControle (
  input  [1:0] op,
  input  clk,
  input  clr,
  output PC_clr,
  output I_rd,
  output [2:0] estA,
  output PC_inc,
  output IR_ld,
  output D_addr,
  output D_rd,
  output RF_s,
  output RF_W_addr,
  output RF_W_wr,
  output D_wr,
  output RF_Rp_addr,
  output RF_Rp_rd,
  output RF_Rq_addr,
  output RF_Rq_rd,
  output alu_s0
);

  wire and_1_out, and_2_out, and_3_out, and_4_out, and_5_out, and_6_out, and_7_out, and_12_out, and_13_out,
       and_16_out, and_17_out, and_18_out, and_19_out, not_1_out, not_2_out, not_3_out, not_4_out, not_5_out;
  wire [2:0] or_3_out;

  not not_1 (not_1_out, estA[2]);
  not not_2 (not_2_out, estA[1]);
  not not_3 (not_3_out, estA[0]);
  not not_4 (not_4_out, op[1]);
  not not_5 (not_5_out, op[0]);
  and and_1 (and_1_out, estA[1], not_3_out, op[0]);
  and and_2 (and_2_out, estA[1], not_3_out, op[1]);
  and and_3 (and_3_out, not_1_out, not_2_out, estA[0]);
  and and_4 (and_4_out, estA[1], not_3_out, not_4_out, not_5_out);
  and and_5 (and_5_out, not_2_out, not_3_out);
  and and_6 (and_6_out, not_3_out, not_5_out);
  and and_7 (and_7_out, estA[1], estA[0]);
  and and_8 (PC_clr, not_1_out, not_2_out, not_3_out);
  and and_9 (I_rd, not_1_out, not_2_out, estA[0]);
  and and_10 (PC_inc, not_1_out, not_2_out, estA[0]);
  and and_11 (IR_ld, not_1_out, not_2_out, estA[0]);
  and and_12 (and_12_out, estA[1], estA[0]);
  and and_13 (and_13_out, estA[2], not_3_out);
  and and_14 (D_rd, estA[1], estA[0]);
  and and_15 (RF_s, estA[1], estA[0]);
  and and_16 (and_16_out, estA[1], estA[0]);
  and and_17 (and_17_out, estA[2], estA[0]);
  and and_18 (and_18_out, estA[1], estA[0]);
  and and_19 (and_19_out, estA[2], estA[0]);
  and and_20 (D_wr, estA[2], not_3_out);
  and and_21 (RF_Rq_addr, estA[2], estA[0]);
  and and_22 (RF_Rq_rd, estA[2], estA[0]);
  and and_23 (alu_s0, estA[2], estA[0]);
  Register #(.width(3)) register_1 (.D(or_3_out), .clk(clk), .Q(estA), .clr(clr));  // open: en
  or or_1 (or_3_out[2], and_1_out, and_2_out);
  or or_2 (or_3_out[1], and_3_out, and_4_out);
  or or_3 (or_3_out[0], and_5_out, and_6_out, and_7_out, estA[2]);
  or or_4 (D_addr, and_12_out, and_13_out);
  or or_5 (RF_W_addr, and_16_out, and_17_out);
  or or_6 (RF_W_wr, and_18_out, and_19_out);

  assign RF_Rp_addr = estA[2];
  assign RF_Rp_rd = estA[2];
endmodule

module UnidadeControle (
  input  [7:0] d,
  input  [3:0] op,
  input  [3:0] ra,
  input  [3:0] rb,
  input  [3:0] rc,
  input  clk,
  input  clr,
  output [7:0] D_addr,
  output [3:0] RF_W_addr,
  output [3:0] RF_Rp_addr,
  output [3:0] RF_Rq_addr,
  output PC_clr,
  output I_rd,
  output PC_inc,
  output IR_ld,
  output D_rd,
  output RF_s,
  output RF_W_wr,
  output D_wr,
  output RF_Rp_rd,
  output RF_Rq_rd,
  output alu_s0
);

  wire comparator_1_eq, comparator_2_eq, fsmcontrole_1_d_addr, fsmcontrole_1_rf_rq_addr,
       fsmcontrole_1_rf_w_addr, nor_1_out;
  wire [1:0] bit_extender_1_out, controlled_buffer_1_out;
  wire [2:0] fsmcontrole_1_esta;

  Bit_Extender #(.in_width(4), .out_width(2)) bit_extender_1 (.in(op), .out(bit_extender_1_out));
  Comparator #(.width(3)) comparator_1 (.a(3'b101), .b(fsmcontrole_1_esta), .eq(comparator_1_eq));  // open: gt, lt
  Comparator #(.width(3)) comparator_2 (.a(fsmcontrole_1_esta), .b(3'b100), .eq(comparator_2_eq));  // open: gt, lt
  assign controlled_buffer_1_out = nor_1_out ? 2'b00 : 2'bz;  // Controlled_Buffer controlled_buffer_1
  nor nor_1 (nor_1_out, comparator_2_eq, comparator_1_eq);
  assign controlled_buffer_1_out = comparator_1_eq ? 2'b10 : 2'bz;  // Controlled_Buffer controlled_buffer_2
  assign controlled_buffer_1_out = comparator_2_eq ? 2'b01 : 2'bz;  // Controlled_Buffer controlled_buffer_3
  FSMControle fsmcontrole_1 (
    .op(bit_extender_1_out), .clk(clk), .clr(clr), .PC_clr(PC_clr), .I_rd(I_rd), .estA(fsmcontrole_1_esta),
    .PC_inc(PC_inc), .IR_ld(IR_ld), .D_addr(fsmcontrole_1_d_addr), .D_rd(D_rd), .RF_s(RF_s),
    .RF_W_addr(fsmcontrole_1_rf_w_addr), .RF_W_wr(RF_W_wr), .D_wr(D_wr), .RF_Rp_rd(RF_Rp_rd),
    .RF_Rq_addr(fsmcontrole_1_rf_rq_addr), .RF_Rq_rd(RF_Rq_rd), .alu_s0(alu_s0));  // open: RF_Rp_addr
  Multiplexer #(.width(8)) multiplexer_1 (.in0({8{1'b0}}), .in1(d), .out(D_addr), .sel(fsmcontrole_1_d_addr));
  Multiplexer #(.width(4)) multiplexer_2 (.in0(4'b0000), .in1(ra), .out(RF_W_addr), .sel(fsmcontrole_1_rf_w_addr));
  Multiplexer #(.select(2), .width(4)) multiplexer_3 (
    .in0(4'b0000), .in1(ra), .in2(rb), .out(RF_Rp_addr), .sel(controlled_buffer_1_out));  // open: in3
  Multiplexer #(.width(4)) multiplexer_4 (.in0(4'b0000), .in1(rc), .out(RF_Rq_addr), .sel(fsmcontrole_1_rf_rq_addr));
endmodule
