// Logisim project R2 - Multiplicação de números sinalizados.circ as structural Verilog: 1 circuit, main circuit main
module main (
  input  [3:0] in_1,
  input  [3:0] in_2,
  input  [3:0] in_3,
  input  in_4,
  output [7:0] out_5
);

  wire [3:0] multiplexer_1_out, multiplexer_2_out, multiplexer_3_out, multiplexer_4_out;
  wire [7:0] adder_1_out, adder_2_out;

  Multiplexer #(.width(4), .enable("false")) multiplexer_1 (
    .in0(in_1), .in1(in_2), .out(multiplexer_1_out), .sel(in_3[0]));
  Multiplexer #(.width(4), .enable("false")) multiplexer_2 (
    .in0(in_1), .in1(in_2), .out(multiplexer_2_out), .sel(in_3[1]));
  Multiplexer #(.width(4), .enable("false")) multiplexer_3 (
    .in0(in_1), .in1(in_2), .out(multiplexer_3_out), .sel(in_3[2]));
  Multiplexer #(.width(4), .enable("false")) multiplexer_4 (
    .in0(in_1), .in1(in_2), .out(multiplexer_4_out), .sel(in_3[3]));
  Adder adder_1 (
    .a({{4{in_4}}, multiplexer_1_out}), .b({{3{in_4}}, multiplexer_2_out, in_4}), .out(adder_1_out));  // open: cin, cout
  Adder adder_2 (
    .a({{2{in_4}}, multiplexer_3_out, {2{in_4}}}), .b({in_4, multiplexer_4_out, {3{in_4}}}), .out(adder_2_out));  // open: cin, cout
  Adder adder_3 (.a(adder_1_out), .b(adder_2_out), .out(out_5));  // open: cin, cout
endmodule
