// Logisim project R2 - Números sinalizados.circ as structural Verilog: 1 circuit, main circuit main
module main (
  input  [3:0] in_1
);

  wire [3:0] multiplexer_1_out, not_1_out, subtractor_1_out;

  Subtractor #(.width(4)) subtractor_1 (.a(in_1), .b(4'b0001), .out(subtractor_1_out));  // open: bin, bout
  not not_1 (not_1_out[0], subtractor_1_out[0]);
  not not_2 (not_1_out[1], subtractor_1_out[1]);
  not not_3 (not_1_out[2], subtractor_1_out[2]);
  not not_4 (not_1_out[3], subtractor_1_out[3]);
  LED led_1 (.in(in_1[3]));
  Hex_Digit_Display hex_digit_display_1 (.value(multiplexer_1_out));  // open: dp
  Multiplexer #(.width(4), .enable("false")) multiplexer_1 (
    .in0(in_1), .in1(not_1_out), .out(multiplexer_1_out), .sel(subtractor_1_out[3]));
endmodule
