// Logisim project SOMADORES.circ as structural Verilog: 2 circuits, main circuit main
module main (
  input  A,
  input  B,
  input  A_2,
  input  B_2,
  input  A_3,
  input  B_3,
  input  Ci,
  input  Ci_2,
  input  A4,
  input  B4,
  input  A3,
  input  B3,
  input  A2,
  input  B2,
  input  A1,
  input  B1,
  input  Ci_3,
  input  A4_2,
  input  B4_2,
  input  A3_2,
  input  B3_2,
  input  A2_2,
  input  B2_2,
  input  A1_2,
  input  B1_2,
  input  Ci_4,
  input  A4_3,
  input  B4_3,
  input  A3_3,
  input  B3_3,
  input  A2_3,
  input  B2_3,
  input  A1_3,
  input  B1_3,
  input  Ci_5,
  input  [7:0] B_4,
  input  [7:0] A_4,
  output out_38,
  output out_39,
  output out_40,
  output Co,
  output Co_2,
  output out_43,
  output Co4,
  output Co3,
  output Co2,
  output Co1,
  output [4:0] out_48,
  output _4,
  output _3,
  output _2,
  output _1,
  output out_53,
  output out_54,
  output out_55,
  output out_56,
  output Co4_2,
  output Co3_2,
  output Co2_2,
  output Co1_2,
  output [4:0] out_61,
  output Co1_3,
  output _4_2,
  output _3_2,
  output _2_2,
  output _1_2,
  output [4:0] out_67,
  output Co1_4,
  output Co1_5,
  output Co1_6,
  output Co1_7,
  output _1_3,
  output _1_4,
  output _1_5,
  output _1_6,
  output [8:0] out_76
);

  wire and_1_out, and_2_out, and_3_out, and_4_out, and_6_out, and_7_out, and_8_out, and_9_out, and_10_out,
       and_11_out, and_12_out, and_13_out, and_14_out, and_15_out, and_16_out, and_17_out, and_18_out,
       and_19_out, and_20_out, and_21_out, Cg1_out, Cg2_out, Cg3_out, Cg4_out, Cp1_out, Cp2_out, Cp3_out,
       Cp4_out, n74283_1_pin7, or_2_out, or_5_out, or_7_out, or_9_out, or_11_out, or_12_out, or_13_out,
       xor_1_out;

  or or_1 (out_53, and_2_out, and_1_out);
  C c_1 (.B(B4), .Ci(Co3), .out_4(_4), .Co(Co4), .A(A4));
  and and_1 (and_1_out, or_2_out, out_54);
  xor xor_1 (xor_1_out, A_2, B_2);
  and and_2 (and_2_out, A4_2, B4_2);
  or or_2 (or_2_out, A4_2, B4_2);
  xor xor_2 (out_40, xor_1_out, Ci_2);
  and and_3 (and_3_out, xor_1_out, Ci_2);
  or or_3 (Co, and_3_out, and_4_out);
  and and_4 (and_4_out, A_2, B_2);
  C c_2 (.B(B3), .Ci(Co2), .out_4(_3), .Co(Co3), .A(A3));
  C c_3 (.B(B4_2), .Ci(out_54), .out_4(_4_2), .Co(Co4_2), .A(A4_2));
  xor xor_3 (out_38, A, B);
  and and_5 (out_39, A, B);
  C c_4 (.B(B2), .Ci(Co1), .out_4(_2), .Co(Co2), .A(A2));
  or or_4 (out_54, and_7_out, and_6_out);
  and and_6 (and_6_out, or_5_out, out_55);
  C c_5 (.B(B1), .Ci(Ci_3), .out_4(_1), .Co(Co1), .A(A1));
  and and_7 (and_7_out, A3_2, B3_2);
  or or_5 (or_5_out, A3_2, B3_2);
  Hex_Digit_Display hex_digit_display_1 (.value(B_4[3:0]));  // open: dp
  Hex_Digit_Display hex_digit_display_2 (.value(B_4[7:4]));  // open: dp
  C c_6 (.B(B_3), .Ci(Ci), .out_4(out_43), .Co(Co_2), .A(A_3));
  C c_7 (.B(B3_2), .Ci(out_55), .out_4(_3_2), .Co(Co3_2), .A(A3_2));
  or or_6 (out_55, and_9_out, and_8_out);
  and and_8 (and_8_out, or_7_out, out_56);
  and and_9 (and_9_out, A2_2, B2_2);
  or or_7 (or_7_out, B2_2, B2_2);
  C c_8 (.B(B2_2), .Ci(out_56), .out_4(_2_2), .Co(Co2_2), .A(A2_2));
  _74283 u_74283_1 (
    .pin1(out_76[5]), .pin2(B_4[5]), .pin3(A_4[5]), .pin4(out_76[4]), .pin5(A_4[4]), .pin6(B_4[4]),
    .pin7(n74283_1_pin7), .pin15(B_4[6]), .pin14(A_4[6]), .pin13(out_76[6]), .pin12(A_4[7]), .pin11(B_4[7]),
    .pin10(out_76[7]), .pin9(out_76[8]));
  or or_8 (out_56, and_11_out, and_10_out);
  and and_10 (and_10_out, or_9_out, Ci_4);
  and and_11 (and_11_out, A1_2, B1_2);
  or or_9 (or_9_out, A1_2, B1_2);
  C c_9 (.B(B1_2), .Ci(Ci_4), .out_4(_1_2), .Co(Co1_2), .A(A1_2));
  _74283 u_74283_2 (
    .pin1(out_76[1]), .pin2(B_4[1]), .pin3(A_4[1]), .pin4(out_76[0]), .pin5(A_4[0]), .pin6(B_4[0]),
    .pin15(B_4[2]), .pin14(A_4[2]), .pin13(out_76[2]), .pin12(A_4[3]), .pin11(B_4[3]), .pin10(out_76[3]),
    .pin9(n74283_1_pin7));  // open: pin7
  Hex_Digit_Display hex_digit_display_3 (.value({3'b000, out_76[8]}));  // open: dp
  Hex_Digit_Display hex_digit_display_4 (.value(out_76[7:4]));  // open: dp
  Hex_Digit_Display hex_digit_display_5 (.value(out_76[3:0]));  // open: dp
  Hex_Digit_Display hex_digit_display_6 (.value(A_4[3:0]));  // open: dp
  Hex_Digit_Display hex_digit_display_7 (.value(A_4[7:4]));  // open: dp
  or or_10 (Co1_3, Cg4_out, and_12_out, and_13_out, and_14_out, and_15_out);
  and and_12 (and_12_out, Cp4_out, Cg3_out);
  and and_13 (and_13_out, Cp4_out, Cg3_out, Cg2_out);
  and and_14 (and_14_out, Cp4_out, Cp3_out, Cg2_out, Cp1_out);
  and and_15 (and_15_out, Cp4_out, Cp3_out, Cp2_out, Cp1_out, Ci_5);
  and Cg4 (Cg4_out, A4_3, B4_3);
  or Cp4 (Cp4_out, A4_3, B4_3);
  or or_11 (or_11_out, Cg3_out, and_16_out, and_17_out, and_18_out);
  C c_10 (.B(B4_3), .Ci(or_11_out), .out_4(_1_6), .Co(Co1_7), .A(A4_3));
  and Cg3 (Cg3_out, A3_3, B3_3);
  or Cp3 (Cp3_out, A3_3, B3_3);
  and and_16 (and_16_out, Cp3_out, Cg2_out);
  and and_17 (and_17_out, Cp3_out, Cp2_out, Cg1_out);
  and and_18 (and_18_out, Cp3_out, Cp2_out, Cg1_out, Ci_5);
  or or_12 (or_12_out, Cg2_out, and_19_out, and_20_out);
  C c_11 (.B(B3_3), .Ci(or_12_out), .out_4(_1_3), .Co(Co1_4), .A(A3_3));
  and and_19 (and_19_out, Cp2_out, Cg1_out);
  and and_20 (and_20_out, Cp2_out, Cp1_out, Ci_5);
  and Cg2 (Cg2_out, A2_3, B2_3);
  or Cp2 (Cp2_out, A2_3, B2_3);
  or or_13 (or_13_out, Cg1_out, and_21_out);
  C c_12 (.B(B2_3), .Ci(or_13_out), .out_4(_1_4), .Co(Co1_5), .A(A2_3));
  and and_21 (and_21_out, Cp1_out, Ci_5);
  and Cg1 (Cg1_out, A1_3, B1_3);
  or Cp1 (Cp1_out, A1_3, B1_3);
  C c_13 (.B(B1_3), .Ci(Ci_5), .out_4(_1_5), .Co(Co1_6), .A(A1_3));

  assign out_48 = {Co4, _4, _3, _2, _1};
  assign out_61 = {Co4_2, _4_2, _3_2, _2_2, _1_2};
  assign out_67 = {Co1_7, _1_6, _1_3, _1_4, _1_5};

  // Notes on the sheet:
  //   SOMADOR PARALELO 4 BITS
  //   MEIO SOMADOR
  //   SOMADOR COMPLETO
  //   SOMADOR DE 8BITS 
  //   Cp4 . Cp3 . Cg2 . Cp1
  //   Cp4 . Cp3 . Cp2 . Cp1 . Ci1
  //   Cp4 . Cg3
  //   Cp4 . Cp3 . Cg2
  //   Cp3 . Cg2
  //   Cp3 . Cp2 . Cg1
  //   Cp3 . Cp2 . Cp1 . Ci1
  //   SOMADOR COM CARRY ANTECIPADO
  //   Cp2 . Cg1
  //   Cp2 . Cp1 . Ci1
  //   Cp1 . Ci1
endmodule

module C (
  input  A,
  input  B,
  input  Ci,
  output out_4,
  output Co
);

  wire and_1_out, and_2_out, xor_1_out;

  xor xor_1 (xor_1_out, A, B);
  and and_1 (and_1_out, xor_1_out, Ci);
  and and_2 (and_2_out, A, B);
  xor xor_2 (out_4, xor_1_out, Ci);
  or or_1 (Co, and_1_out, and_2_out);
endmodule
