// Logisim project Somador Completo 4 bits.circ as structural Verilog: 3 circuits, main circuit Somadores
module Somadores (
  input  A0,
  input  B0,
  input  A1,
  input  B1,
  input  A2,
  input  Ci,
  input  B2,
  input  A3,
  input  B3,
  output S3,
  output S2,
  output S1,
  output S0,
  output Co
);

  wire somador_2_co, somador_3_co, somador_4_co;

  Somador somador_1 (.Ci(somador_2_co), .A(A3), .B(B3), .Co(Co), .S(S3));
  Somador somador_2 (.Ci(somador_3_co), .A(A2), .B(B2), .Co(somador_2_co), .S(S2));
  Somador somador_3 (.Ci(somador_4_co), .A(A1), .B(B1), .Co(somador_3_co), .S(S1));
  Somador somador_4 (.Ci(Ci), .A(A0), .B(B0), .Co(somador_4_co), .S(S0));
endmodule

module Somador (
  input  Ci,
  input  A,
  input  B,
  output Co,
  output S
);

  wire and_1_out, and_2_out, and_3_out, and_4_out, and_5_out, and_6_out, and_7_out, not_1_out, not_2_out,
       not_3_out, not_4_out, not_5_out, not_6_out;

  and and_1 (and_1_out, A, B);
  and and_2 (and_2_out, Ci, B);
  and and_3 (and_3_out, Ci, A);
  not not_1 (not_1_out, Ci);
  not not_2 (not_2_out, A);
  not not_3 (not_3_out, Ci);
  not not_4 (not_4_out, B);
  not not_5 (not_5_out, A);
  not not_6 (not_6_out, B);
  or or_1 (Co, and_1_out, and_2_out, and_3_out);
  and and_4 (and_4_out, not_1_out, not_2_out, B);
  and and_5 (and_5_out, not_3_out, A, not_4_out);
  and and_6 (and_6_out, Ci, not_5_out, not_6_out);
  and and_7 (and_7_out, Ci, A, B);
  or or_2 (S, and_4_out, and_5_out, and_6_out, and_7_out);
endmodule

module test (
  input  [3:0] A,
  input  [3:0] B,
  input  in_3,
  output [3:0] out_4,
  output out_5
);

  Somadores somadores_1 (
    .A0(A[0]), .B0(B[0]), .A1(A[1]), .B1(B[1]), .A2(A[2]), .B2(B[2]), .A3(A[3]), .Ci(in_3), .B3(B[3]),
    .Co(out_5), .S3(out_4[3]), .S2(out_4[2]), .S1(out_4[1]), .S0(out_4[0]));
endmodule
