// Logisim project contadorDecada4bits.circ as structural Verilog: 1 circuit, main circuit main
module main (
);

  wire and_1_out, and_2_out, and_3_out, and_4_out, clock_1_out, digital_oscilloscope_1_p3,
       digital_oscilloscope_1_p4, digital_oscilloscope_1_p5, digital_oscilloscope_1_p6, j_k_ff_1_q,
       j_k_ff_4_qn, or_1_out;

  Clock clock_1 (.out(clock_1_out));
  J_K_Flip_Flop #(.trigger("falling")) j_k_ff_1 (
    .J(1'b1), .clk(clock_1_out), .K(1'b1), .Q(j_k_ff_1_q));  // open: Qn, preset, reset
  // Digital_Oscilloscope digital_oscilloscope_1: pin names not known; wires that end beside it: clock_1_out, j_k_ff_1_q, digital_oscilloscope_1_p3, digital_oscilloscope_1_p4, digital_oscilloscope_1_p5, digital_oscilloscope_1_p6
  Button button_1 (.out(digital_oscilloscope_1_p6));
  and and_1 (and_1_out, j_k_ff_1_q, j_k_ff_4_qn);
  and and_2 (and_2_out, j_k_ff_1_q, digital_oscilloscope_1_p3);
  J_K_Flip_Flop #(.trigger("falling")) j_k_ff_2 (
    .J(and_1_out), .clk(clock_1_out), .K(and_1_out), .Q(digital_oscilloscope_1_p3));  // open: Qn, preset, reset
  J_K_Flip_Flop #(.trigger("falling")) j_k_ff_3 (
    .J(and_2_out), .clk(clock_1_out), .K(and_2_out), .Q(digital_oscilloscope_1_p4));  // open: Qn, preset, reset
  and and_3 (and_3_out, digital_oscilloscope_1_p5, j_k_ff_1_q);
  or or_1 (or_1_out, and_3_out, and_4_out);
  and and_4 (and_4_out, and_2_out, digital_oscilloscope_1_p4);
  J_K_Flip_Flop #(.trigger("falling")) j_k_ff_4 (
    .J(or_1_out), .clk(clock_1_out), .K(or_1_out), .Q(digital_oscilloscope_1_p5), .Qn(j_k_ff_4_qn));  // open: preset, reset

  // Notes on the sheet:
  //   clk
  //   Q0
  //   Q1
  //   Q2
  //   Q3
  //   Q3'
endmodule
