// Logisim project medidorDistanciaRaioLaser.circ as structural Verilog: 4 circuits, main circuit main
module main (
  output L,
  output [15:0] D
);

  wire B_out, clock_1_out, Controle_d_clr, Controle_d_cnt, Controle_r_clr, Controle_r_ld, S_out;

  Button S (.out(S_out));
  Button B (.out(B_out));
  Clock clock_1 (.out(clock_1_out));
  controle Controle (
    .B(B_out), .S(S_out), .clk(clock_1_out), .L(L), .r_ld(Controle_r_ld), .r_clr(Controle_r_clr),
    .d_cnt(Controle_d_cnt), .d_clr(Controle_d_clr));
  operacional Operacional (
    .d_cnt(Controle_d_cnt), .clk(clock_1_out), .d_clr(Controle_d_clr), .r_ld(Controle_r_ld),
    .r_clr(Controle_r_clr), .D(D));
endmodule

module operacional (
  input  d_cnt,
  input  clk,
  input  d_clr,
  input  r_ld,
  input  r_clr,
  output [15:0] D
);

  wire [15:0] counter_1_q, shifter_1_out;

  Counter #(.width(16), .max('hffff)) counter_1 (
    .count(d_cnt), .Q(counter_1_q), .clk(clk), .clr(d_clr));  // open: load, D, carry, preset, down
  Shifter #(.width(16)) shifter_1 (.in(counter_1_q), .\dist (4'b0001), .out(shifter_1_out));
  Register #(.width(16), .Select("low")) register_1 (.D(shifter_1_out), .en(r_ld), .Q(D), .clk(clk), .clr(r_clr));
endmodule

module controle (
  input  B,
  input  S,
  input  clk,
  output L,
  output r_ld,
  output r_clr,
  output d_cnt,
  output d_clr
);

  wire [2:0] fsmcontrole_1_n0, register_1_q;

  fsmcontrole fsmcontrole_1 (
    .s2(register_1_q[2]), .s1(register_1_q[1]), .s0(register_1_q[0]), .b(B), .s(S), .n2(fsmcontrole_1_n0[2]),
    .n1(fsmcontrole_1_n0[1]), .n0(fsmcontrole_1_n0[0]), .l(L), .r_ld(r_ld), .r_clr(r_clr), .d_cnt(d_cnt),
    .d_clr(d_clr));
  Register #(.width(3), .Select("low")) register_1 (
    .D(fsmcontrole_1_n0), .Q(register_1_q), .clk(clk));  // open: en, clr
endmodule

module fsmcontrole (
  input  s2,
  input  s1,
  input  s0,
  input  b,
  input  s,
  output n2,
  output n1,
  output n0,
  output l,
  output r_ld,
  output r_clr,
  output d_cnt,
  output d_clr
);

  wire and_2_out, and_3_out, and_4_out, and_5_out, and_6_out, and_7_out, and_8_out, not_1_out, not_2_out,
       not_3_out, not_4_out, not_5_out, not_6_out, not_7_out, not_8_out, not_9_out, not_10_out, not_11_out,
       not_12_out, not_13_out, not_14_out, not_15_out, not_16_out, not_17_out, not_18_out, not_19_out,
       not_20_out, not_21_out, not_22_out, not_23_out, not_24_out, not_25_out, not_26_out;

  not not_1 (not_1_out, s2);
  not not_2 (not_2_out, s2);
  not not_3 (not_3_out, s1);
  not not_4 (not_4_out, s2);
  not not_5 (not_5_out, s0);
  not not_6 (not_6_out, s2);
  not not_7 (not_7_out, s);
  not not_8 (not_8_out, s2);
  not not_9 (not_9_out, s1);
  not not_10 (not_10_out, b);
  not not_11 (not_11_out, s2);
  not not_12 (not_12_out, s0);
  not not_13 (not_13_out, s1);
  not not_14 (not_14_out, s0);
  not not_15 (not_15_out, s2);
  not not_16 (not_16_out, s);
  not not_17 (not_17_out, s2);
  not not_18 (not_18_out, s0);
  not not_19 (not_19_out, s1);
  not not_20 (not_20_out, s0);
  not not_21 (not_21_out, s2);
  not not_22 (not_22_out, s1);
  not not_23 (not_23_out, s0);
  not not_24 (not_24_out, s2);
  not not_25 (not_25_out, s2);
  not not_26 (not_26_out, s1);
  and and_1 (n2, not_1_out, s1, s0, s);
  and and_2 (and_2_out, not_2_out, not_3_out, s0, b);
  and and_3 (and_3_out, not_4_out, s1, not_5_out);
  and and_4 (and_4_out, not_6_out, s1, not_7_out);
  and and_5 (and_5_out, not_8_out, not_9_out, not_10_out);
  and and_6 (and_6_out, not_11_out, not_12_out);
  and and_7 (and_7_out, not_13_out, not_14_out);
  and and_8 (and_8_out, not_15_out, s1, not_16_out);
  and and_9 (l, not_17_out, s1, not_18_out);
  and and_10 (r_ld, s2, not_19_out, not_20_out);
  and and_11 (r_clr, not_21_out, not_22_out, not_23_out);
  and and_12 (d_cnt, not_24_out, s1, s0);
  and and_13 (d_clr, not_25_out, not_26_out, s0);
  or or_1 (n1, and_2_out, and_3_out, and_4_out);
  or or_2 (n0, and_5_out, and_6_out, and_7_out, and_8_out);
endmodule
